// Logisim project cpu.circ as structural Verilog: 1 circuit, main circuit cpu
module cpu (
  input  clk,
  input  [31:0] Instruction,
  input  [31:0] MemReadData,
  output [31:0] MemAddress,
  output [31:0] ProgramCounter,
  output [31:0] ra,
  output [31:0] sp,
  output [31:0] t0,
  output [31:0] t1,
  output [31:0] t2,
  output [31:0] s0,
  output [31:0] s1,
  output [31:0] a0,
  output [3:0] MemWriteMask,
  output [31:0] MemWriteData
);

  wire [2:0] control_logic_1_immsel;
  wire [31:0] adder_1_out, ALURes, imm_gen_1_immediate, multiplexer_1_out, regfile_1_readdata1,
       regfile_1_readdata2;

  Register #(.width(32)) PC (.D(adder_1_out), .clk(clk), .Q(ProgramCounter));  // open: en, clr
  Adder #(.width(32)) adder_1 (.a(ProgramCounter), .b(32'h4), .out(adder_1_out));  // open: cin, cout
  control_logic control_logic_1 (.ImmSel(control_logic_1_immsel));  // open: Instruction, BrEq, BrLt, PCSel, RegWEn, BrUn, ASel, BSel, ALUSel, MemWEn, WBSel
  regfile regfile_1 (
    .ReadIndex1(Instruction[19:15]), .WriteIndex(Instruction[11:7]), .WriteData(ALURes), .RegWEn(1'b1),
    .clk(clk), .ra(ra), .sp(sp), .t0(t0), .t1(t1), .t2(t2), .s0(s0), .s1(s1), .a0(a0),
    .ReadData1(regfile_1_readdata1), .ReadData2(regfile_1_readdata2));  // open: ReadIndex2
  Multiplexer #(.width(32)) multiplexer_1 (
    .in0(regfile_1_readdata2), .in1(imm_gen_1_immediate), .out(multiplexer_1_out), .sel(1'b1));
  imm_gen imm_gen_1 (.Instruction(Instruction), .ImmSel(control_logic_1_immsel), .Immediate(imm_gen_1_immediate));
  alu alu_1 (.A(regfile_1_readdata1), .B(multiplexer_1_out), .ALUSel(4'b0000), .ALUResult(ALURes));
  // partial_store partial_store_1: pin names not known
  // partial_load partial_load_1: pin names not known
  // branch_comp branch_comp_1: pin names not known

  // Other names for the same wires on the sheet: IWrite[4:0] = Instruction[11:7]; IRead[4:0] = Instruction[19:15]

  // Notes on the sheet:
  //   To IMEM
  //   IMEM (do **NOT** move this)
  //   From IMEM
  //   Inputs/Outputs for testing. Do **NOT** move these.
  //   It is OK to move the PC, RegFile, ALU, MEM, Branch Comp, Imm Gen, Partial Load, Partial Store and Control Logic to wherever is most convenient for you when constructing your CPU, and to delete this text
  //   To DMEM
  //   DMEM (do **NOT** move this)
  //   From DMEM
endmodule
